// Digital circuit spiden.dig as structural Verilog
module spiden (
  input  spi_miso,
  input  [15:0] Address,
  input  clk,
  input  st,
  input  [15:0] DataIn,
  input  ld,
  input  spi_rst,
  output spi_clk,
  output spi_mosi,
  output Busy,
  output [15:0] data_out
);

  wire and_1_out, and_2_out, and_4_out, and_5_out, and_6_out, and_7_out, and_8_out, and_9_out, and_10_out,
       and_11_out, and_12_out, busy_N, busy_t, load, multiplexer_3_out, or_2_out, or_3_out, or_4_out,
       Reset_q, rstSpi, Rx_Ready, Selected, store, Tx_Ready, xor_1_out;
  wire [2:0] counter_1_out, sub_1_s;
  wire [7:0] data_Rx, multiplexer_1_out, multiplexer_2_out, ramAdres_0, ramAdres_1, ramData_0, ramData_1;

  and and_1 (and_1_out, st, clk);
  and and_2 (and_2_out, ld, clk);
  and and_3 (Busy, ~rstSpi, Selected);  // And
  Register #(.Bits(16)) RamAddress (.D(Address), .C(clk), .en(Selected), .Q({ramAdres_1, ramAdres_0}));
  Register #(.Bits(16)) RamData (.D(DataIn), .C(clk), .en(Selected), .Q({ramData_1, ramData_0}));
  or or_1 (Selected, load, store);
  and and_4 (and_4_out, rstSpi, ~st);  // And
  and and_5 (and_5_out, rstSpi, ~ld);  // And
  D_FF_AS d_ff_as_1 (.Set(and_1_out), .D(store), .C(1'b1), .Clr(and_4_out), .Q(store));  // open: nQ
  D_FF_AS d_ff_as_2 (.Set(and_2_out), .D(load), .C(1'b1), .Clr(and_5_out), .Q(load));  // open: nQ
  or or_2 (or_2_out, Tx_Ready, rstSpi);
  Counter #(.Bits(3)) counter_1 (.en(1'b1), .C(or_2_out), .clr(rstSpi), .out(counter_1_out));  // open: ovf
  Sub #(.Bits(3)) sub_1 (.a(counter_1_out), .b(3'b001), .c_i(1'b0), .s(sub_1_s));  // open: c_o
  Multiplexer #(.Selector_Bits(3), .Bits(8)) multiplexer_1 (
    .sel(sub_1_s), .in_0({7'b0000001, load}), .in_1(ramAdres_1), .in_2(ramAdres_0), .in_3(ramData_1),
    .in_4(ramData_0), .in_5({8{1'b0}}), .in_6({8{1'b0}}), .in_7({8{1'b0}}), .out(multiplexer_1_out));
  and and_6 (and_6_out, sub_1_s[0], sub_1_s[1], ~sub_1_s[2]);  // And
  Multiplexer #(.Bits(8)) multiplexer_2 (
    .sel(and_12_out), .in_0(multiplexer_1_out), .in_1({8{1'b0}}), .out(multiplexer_2_out));
  and and_7 (and_7_out, ~sub_1_s[0], ~sub_1_s[1], sub_1_s[2]);  // And
  and and_8 (and_8_out, sub_1_s[2], ~sub_1_s[1], ~sub_1_s[0]);  // And
  or or_3 (or_3_out, and_8_out, and_6_out);
  and and_9 (and_9_out, and_8_out, load);
  and and_10 (and_10_out, and_6_out, load);
  and and_11 (and_11_out, and_8_out, load);
  and and_12 (and_12_out, or_3_out, load);
  or or_4 (or_4_out, and_7_out, and_11_out);
  nand nand_1 (busy_t, Rx_Ready, or_4_out);
  Register #(.Bits(8)) register_1 (.D(data_Rx), .C(Rx_Ready), .en(and_9_out), .Q(data_out[7:0]));
  Register #(.Bits(8)) register_2 (.D(data_Rx), .C(Rx_Ready), .en(and_10_out), .Q(data_out[15:8]));
  Multiplexer multiplexer_3 (.sel(rstSpi), .in_0(Selected), .in_1(1'b0), .out(multiplexer_3_out));
  SPI_Master #(.applicationType("IVERILOG"), .CodeFile("D:\\Desktop\\fpga\\RemedyCpu\\verilog\\SPIs_Master.v")) u_SPI_Master (
    .i_Rst_L(multiplexer_3_out), .i_Clk(clk), .i_TX_Byte(multiplexer_2_out), .i_TX_DV(Tx_Ready),
    .i_SPI_MISO(spi_miso), .o_TX_Ready(Tx_Ready), .o_RX_DV(Rx_Ready), .o_RX_Byte(data_Rx),
    .o_SPI_Clk(spi_clk), .o_SPI_MOSI(spi_mosi));
  not not_1 (busy_N, busy_t);
  JK_FF Reset (.J(busy_N), .C(clk), .K(xor_1_out), .Q(Reset_q));  // open: nQ
  xor xor_1 (xor_1_out, Selected, rstSpi);
  or or_5 (rstSpi, spi_rst, Reset_q);

  // Other names for the same wires on the sheet: data_outSpi[15:0] = data_out; ramCommand[0] = load

  // Notes on the sheet:
  //   Address: default 65534
endmodule
