// Digital circuit Alu.dig as structural Verilog
module Alu (
  input  [15:0] A,
  input  [15:0] B,
  input  carryIn,
  input  [4:0] AluOp,
  output [15:0] Out,
  output Neg,
  output Zero,
  output CarryOut
);

  wire add_1_c_o, sub_1_c_o;
  wire [15:0] add_1_s, and_2_out, divs_1_bolum, divs_1_kalan, mul_1_mul, neg_1_out, not_1_out, or_1_out,
       sub_1_s, xor_1_out;
  wire [15:15] and_1_out;
  wire [31:16] mul_1_mul_2;

  and and_1 (and_1_out[15], AluOp[4], carryIn);
  divs divs_1 (.bolunen(B), .Bolen(A), .bolum(divs_1_bolum), .Kalan(divs_1_kalan));
  Add #(.Bits(16)) add_1 (.a(B), .b(A), .c_i(and_1_out[15]), .s(add_1_s), .c_o(add_1_c_o));
  Sub #(.Bits(16)) sub_1 (.a(B), .b(A), .c_i(and_1_out[15]), .s(sub_1_s), .c_o(sub_1_c_o));
  assign and_2_out = B & A;  // And and_2, 16 bits wide
  assign or_1_out = B | A;  // Or or_1, 16 bits wide
  assign xor_1_out = B ^ A;  // XOr xor_1, 16 bits wide
  assign not_1_out = ~B;  // Not not_1, 16 bits wide
  Neg #(.Bits(16)) neg_1 (.in(B), .out(neg_1_out));
  Mul #(.Bits(16)) mul_1 (.a(B), .b(A), .mul({mul_1_mul_2, mul_1_mul}));
  Multiplexer #(.Selector_Bits(4), .Bits(16)) multiplexer_1 (
    .sel(AluOp[3:0]), .in_0(A), .in_1(add_1_s), .in_2(sub_1_s), .in_3(and_2_out), .in_4(or_1_out),
    .in_5(xor_1_out), .in_6(not_1_out), .in_7(neg_1_out), .in_8({B[14:0], and_1_out[15]}),
    .in_9({and_1_out[15], B[15:1]}), .in_10({{2{B[15]}}, B[14:1]}), .in_11({B[7:0], B[15:8]}),
    .in_12({B[11:8], B[15:12], B[3:0], B[7:4]}), .in_13(mul_1_mul), .in_14(divs_1_bolum),
    .in_15(divs_1_kalan), .out({Neg, Out[14:0]}));
  Multiplexer #(.Selector_Bits(4)) multiplexer_2 (
    .sel(AluOp[3:0]), .in_0(1'b0), .in_1(add_1_c_o), .in_2(sub_1_c_o), .in_3(1'b0), .in_4(1'b0), .in_5(1'b0),
    .in_6(1'b0), .in_7(1'b0), .in_8(B[15]), .in_9(B[0]), .in_10(B[0]), .in_11(1'b0), .in_12(1'b0),
    .in_13(1'b0), .in_14(1'b0), .in_15(1'b0), .out(CarryOut));
  Comparator #(.Signed("true"), .Bits(16)) comparator_1 (
    .a({Neg, Out[14:0]}), .b({16{1'b0}}), .eq(Zero));  // open: gt, lt

  assign Out[15] = Neg;

  // Other names for the same wires on the sheet: sel[3:0] = AluOp[3:0]

  // Notes on the sheet:
  //   ALU
  //   logical shift left
  //   logical shift right
  //   arithmetic shift right
  //   swapBytes
  //   swapNibbles
endmodule
