// Digital circuit controllogic.dig as structural Verilog
module controllogic (
  input  A,
  input  B,
  input  C,
  input  D,
  input  E,
  input  F,
  input  G,
  output muxb0,
  output muxb1,
  output muxb2,
  output aluop0,
  output aluop1,
  output aluop2,
  output aluop3,
  output aluop4,
  output aluop5,
  output WE,
  output sf,
  output iem0,
  output iem1,
  output br0,
  output br1,
  output br2,
  output muxA,
  output ld,
  output st,
  output abs,
  output ioW,
  output ioR,
  output stPC,
  output Reti,
  output randomSel,
  output timerSel,
  output read_flags,
  output storeFlagI
);

  wire and_1_out, and_2_out, and_3_out, and_4_out, and_5_out, and_6_out, and_7_out, and_8_out, and_9_out,
       and_10_out, and_11_out, and_12_out, and_13_out, and_14_out, and_15_out, and_16_out, and_17_out,
       and_18_out, and_19_out, and_20_out, and_21_out, and_22_out, and_23_out, and_24_out, and_25_out,
       and_26_out, and_27_out, and_28_out, and_29_out, and_30_out, and_31_out, and_32_out, and_33_out,
       and_34_out, and_35_out, and_36_out, and_37_out, and_38_out, and_39_out, and_40_out, and_41_out,
       and_42_out, and_43_out, and_44_out, and_45_out, and_46_out, and_47_out, and_48_out, and_49_out,
       and_50_out, and_51_out, and_52_out, and_53_out, and_54_out, and_55_out, and_56_out, and_57_out,
       and_58_out, and_59_out, and_60_out, and_61_out, and_62_out, and_63_out, and_64_out, and_65_out,
       and_66_out, and_67_out, and_68_out, and_69_out, and_70_out, and_71_out, and_72_out, and_73_out,
       and_74_out, and_75_out, and_76_out, and_77_out, and_78_out, and_79_out, and_80_out, and_81_out,
       and_82_out, and_83_out, and_84_out, and_85_out, and_86_out, and_87_out, and_88_out, and_89_out,
       and_90_out, and_91_out, and_92_out, and_93_out, and_94_out, and_95_out, and_96_out, and_97_out,
       and_98_out, and_99_out, and_100_out, and_101_out, and_102_out, and_103_out, and_104_out, and_105_out,
       and_106_out, and_107_out, and_108_out, and_109_out, and_110_out, and_111_out, and_112_out,
       and_113_out, and_114_out, and_115_out, and_116_out, and_117_out, and_118_out, and_119_out,
       and_120_out, and_121_out, and_122_out, and_123_out, and_124_out, and_125_out, and_126_out,
       and_127_out, and_128_out, and_129_out, and_130_out, and_131_out, and_132_out, and_133_out,
       and_134_out, and_135_out, and_136_out, and_137_out, and_138_out, and_139_out, and_140_out,
       and_141_out, and_142_out, and_143_out, and_144_out, and_145_out, and_146_out, and_147_out,
       and_148_out, and_149_out, and_150_out, and_151_out, and_152_out, and_153_out, and_154_out,
       and_155_out, not_1_out, not_2_out, not_3_out, not_4_out, not_5_out, not_6_out, not_7_out;

  not not_1 (not_1_out, A);
  not not_2 (not_2_out, B);
  not not_3 (not_3_out, C);
  not not_4 (not_4_out, D);
  not not_5 (not_5_out, E);
  not not_6 (not_6_out, F);
  not not_7 (not_7_out, G);
  and and_1 (and_1_out, A, not_2_out, not_3_out, not_4_out, not_5_out, F, not_7_out);
  and and_2 (and_2_out, not_1_out, not_3_out, D, E, F, not_7_out);
  and and_3 (and_3_out, not_1_out, B, C, not_5_out, not_6_out, not_7_out);
  and and_4 (and_4_out, A, not_2_out, not_3_out, E, F, G);
  and and_5 (and_5_out, not_1_out, not_2_out, not_3_out, D, F, not_7_out);
  and and_6 (and_6_out, A, not_2_out, not_3_out, D, not_6_out, G);
  and and_7 (and_7_out, not_1_out, not_2_out, not_3_out, D, E, not_7_out);
  and and_8 (and_8_out, not_1_out, not_2_out, C, not_4_out, not_5_out, not_7_out);
  and and_9 (and_9_out, not_1_out, B, not_3_out, not_4_out, not_5_out, G);
  and and_10 (and_10_out, A, not_2_out, not_3_out, D, not_5_out, not_6_out);
  and and_11 (and_11_out, not_1_out, C, D, not_6_out, G);
  and and_12 (and_12_out, not_1_out, C, not_4_out, E, G);
  and and_13 (and_13_out, not_1_out, B, C, E, G);
  and and_14 (and_14_out, not_1_out, B, C, not_4_out, E);
  and and_15 (and_15_out, not_1_out, C, not_4_out, not_5_out, not_6_out, G);
  and and_16 (and_16_out, A, not_2_out, not_4_out, not_5_out, not_6_out, not_7_out);
  and and_17 (and_17_out, not_1_out, B, not_3_out, not_4_out, not_5_out, not_7_out);
  and and_18 (and_18_out, A, not_2_out, not_3_out, not_4_out, not_5_out, G);
  and and_19 (and_19_out, A, not_2_out, not_3_out, D, E, not_7_out);
  and and_20 (and_20_out, not_1_out, not_3_out, D, F, G);
  and and_21 (and_21_out, not_1_out, C, D, not_6_out, not_7_out);
  and and_22 (and_22_out, not_1_out, B, C, not_6_out, G);
  and and_23 (and_23_out, not_1_out, B, C, F, not_7_out);
  and and_24 (and_24_out, not_1_out, C, not_4_out, E, not_7_out);
  and and_25 (and_25_out, not_1_out, not_2_out, not_3_out, D, G);
  and and_26 (and_26_out, A, not_2_out, not_3_out, not_5_out, not_6_out);
  and and_27 (and_27_out, not_1_out, B, D, E);
  and and_28 (and_28_out, not_1_out, B, C, E);
  and and_29 (and_29_out, not_1_out, B, C, D, E, F, G);
  and and_30 (and_30_out, not_1_out, C, not_4_out, not_5_out, not_6_out, not_7_out);
  and and_31 (and_31_out, not_1_out, B, not_4_out, not_5_out, F, G);
  and and_32 (and_32_out, not_1_out, B, not_3_out, not_5_out, F, G);
  and and_33 (and_33_out, not_1_out, not_2_out, not_3_out, D, F, not_7_out);
  and and_34 (and_34_out, not_1_out, not_2_out, C, D, not_6_out, G);
  and and_35 (and_35_out, A, not_2_out, not_3_out, not_4_out, F, G);
  and and_36 (and_36_out, not_1_out, not_2_out, C, not_4_out, not_5_out, not_7_out);
  and and_37 (and_37_out, not_1_out, not_2_out, C, not_4_out, E, G);
  and and_38 (and_38_out, not_1_out, B, not_3_out, not_4_out, not_5_out, G);
  and and_39 (and_39_out, A, not_2_out, not_3_out, not_4_out, not_5_out, not_7_out);
  and and_40 (and_40_out, A, not_2_out, not_3_out, D, E, G);
  and and_41 (and_41_out, not_1_out, not_3_out, D, E, not_7_out);
  and and_42 (and_42_out, not_1_out, not_2_out, not_3_out, D, E, F, not_7_out);
  and and_43 (and_43_out, not_1_out, not_2_out, C, not_4_out, not_5_out, not_6_out, G);
  and and_44 (and_44_out, not_1_out, not_2_out, C, not_4_out, not_5_out, F, not_7_out);
  and and_45 (and_45_out, not_1_out, not_2_out, C, D, E, F, G);
  and and_46 (and_46_out, not_1_out, not_3_out, not_4_out, not_5_out, F, G);
  and and_47 (and_47_out, not_1_out, not_2_out, not_3_out, E, not_6_out, G);
  and and_48 (and_48_out, not_1_out, B, not_3_out, not_4_out, F);
  and and_49 (and_49_out, not_1_out, not_2_out, C, D, not_5_out, F, G);
  and and_50 (and_50_out, not_1_out, B, not_3_out, D, not_5_out, not_7_out);
  and and_51 (and_51_out, not_1_out, not_2_out, C, D, E, not_6_out);
  and and_52 (and_52_out, not_1_out, B, not_3_out, D, not_5_out, not_6_out);
  and and_53 (and_53_out, A, not_2_out, not_3_out, D, F);
  and and_54 (and_54_out, not_1_out, B, not_3_out, not_4_out, E);
  and and_55 (and_55_out, A, not_2_out, not_3_out, D, E);
  and and_56 (and_56_out, not_1_out, B, not_3_out, D, not_5_out, F, not_7_out);
  and and_57 (and_57_out, not_1_out, not_2_out, not_4_out, E, F, G);
  and and_58 (and_58_out, not_1_out, not_2_out, D, not_5_out, not_6_out, not_7_out);
  and and_59 (and_59_out, not_1_out, not_2_out, C, not_5_out, F, G);
  and and_60 (and_60_out, not_1_out, not_2_out, C, not_4_out, E, F);
  and and_61 (and_61_out, not_1_out, not_2_out, C, D, not_6_out);
  and and_62 (and_62_out, A, not_2_out, not_3_out, D, F);
  and and_63 (and_63_out, not_1_out, not_2_out, C, D, not_5_out);
  and and_64 (and_64_out, A, not_2_out, not_3_out, D, E);
  and and_65 (and_65_out, not_1_out, not_2_out, D, E, F, G);
  and and_66 (and_66_out, not_1_out, not_2_out, C, D, F, not_7_out);
  and and_67 (and_67_out, not_1_out, not_2_out, not_3_out, not_4_out, E, not_7_out);
  and and_68 (and_68_out, not_1_out, not_2_out, not_4_out, E, not_6_out);
  and and_69 (and_69_out, not_1_out, B, not_3_out, not_5_out, not_6_out);
  and and_70 (and_70_out, A, not_2_out, not_3_out, D, F);
  and and_71 (and_71_out, not_1_out, not_2_out, C, not_4_out, not_5_out);
  and and_72 (and_72_out, not_1_out, B, not_3_out, not_4_out, not_5_out);
  and and_73 (and_73_out, A, not_2_out, not_3_out, D, E);
  and and_74 (and_74_out, not_1_out, B, C, not_4_out, not_5_out, not_6_out, G);
  and and_75 (and_75_out, not_1_out, B, C, not_4_out, not_5_out, F, not_7_out);
  and and_76 (and_76_out, A, not_2_out, not_3_out, not_4_out, not_5_out, not_6_out, not_7_out);
  and and_77 (and_77_out, not_1_out, not_3_out, D, E, not_6_out, not_7_out);
  and and_78 (and_78_out, not_1_out, not_2_out, not_3_out, not_4_out, F, not_7_out);
  and and_79 (and_79_out, not_1_out, not_2_out, C, D, not_5_out, G);
  and and_80 (and_80_out, not_1_out, B, not_3_out, not_4_out, E, G);
  and and_81 (and_81_out, not_1_out, B, not_3_out, D, not_5_out, G);
  and and_82 (and_82_out, A, not_2_out, not_3_out, D, E, F);
  and and_83 (and_83_out, not_1_out, not_2_out, not_5_out, F, G);
  and and_84 (and_84_out, not_1_out, not_2_out, D, not_6_out, not_7_out);
  and and_85 (and_85_out, not_1_out, not_2_out, D, E, not_6_out);
  and and_86 (and_86_out, not_1_out, not_2_out, C, E, not_6_out);
  and and_87 (and_87_out, not_2_out, not_3_out, D, E, F, not_7_out);
  and and_88 (and_88_out, not_2_out, not_3_out, not_5_out, F, G);
  and and_89 (and_89_out, not_1_out, D, not_5_out, F, not_7_out);
  and and_90 (and_90_out, not_1_out, not_3_out, E, not_6_out, not_7_out);
  and and_91 (and_91_out, not_1_out, not_3_out, E, F, G);
  and and_92 (and_92_out, not_1_out, C, not_4_out, not_5_out, not_7_out);
  and and_93 (and_93_out, not_1_out, not_3_out, D, not_5_out, not_6_out);
  and and_94 (and_94_out, not_1_out, C, not_4_out, not_5_out, F);
  and and_95 (and_95_out, not_1_out, not_2_out, C, not_6_out);
  and and_96 (and_96_out, not_1_out, not_3_out, not_4_out, E);
  and and_97 (and_97_out, not_1_out, not_2_out, C, not_5_out);
  and and_98 (and_98_out, not_1_out, not_2_out, C, not_4_out);
  and and_99 (and_99_out, not_2_out, not_3_out, not_4_out, not_5_out, G);
  and and_100 (and_100_out, not_2_out, not_3_out, F, G);
  and and_101 (and_101_out, not_2_out, not_3_out, D, not_7_out);
  and and_102 (and_102_out, not_2_out, not_3_out, not_5_out, F);
  and and_103 (and_103_out, not_2_out, not_3_out, D, E);
  and and_104 (and_104_out, not_1_out, not_3_out, D, not_5_out, not_6_out, not_7_out);
  and and_105 (and_105_out, A, not_2_out, not_3_out, D, not_6_out, G);
  and and_106 (and_106_out, A, not_2_out, not_3_out, D, not_5_out, F);
  and and_107 (and_107_out, not_1_out, not_2_out, not_4_out, F, not_7_out);
  and and_108 (and_108_out, not_1_out, not_2_out, D, F, G);
  and and_109 (and_109_out, not_1_out, not_2_out, not_3_out, F, G);
  and and_110 (and_110_out, not_1_out, not_2_out, C, not_6_out);
  and and_111 (and_111_out, not_1_out, B, not_3_out, not_4_out);
  and and_112 (and_112_out, not_1_out, not_2_out, E);
  and and_113 (and_113_out, not_2_out, not_3_out, D, E, not_7_out);
  and and_114 (and_114_out, not_1_out, not_2_out, C, not_4_out, not_5_out, not_6_out, G);
  and and_115 (and_115_out, A, not_2_out, not_3_out, not_4_out, not_5_out, not_6_out, G);
  and and_116 (and_116_out, A, not_2_out, C, not_4_out, not_5_out, not_6_out, not_7_out);
  and and_117 (and_117_out, not_1_out, C, D, E, not_6_out, not_7_out);
  and and_118 (and_118_out, A, not_2_out, not_3_out, E, F, not_7_out);
  and and_119 (and_119_out, not_1_out, not_2_out, C, D, not_6_out, not_7_out);
  and and_120 (and_120_out, not_1_out, B, C, D, F, not_7_out);
  and and_121 (and_121_out, not_1_out, not_2_out, C, not_4_out, E, not_7_out);
  and and_122 (and_122_out, not_1_out, B, not_3_out, not_4_out, not_5_out, not_7_out);
  and and_123 (and_123_out, A, not_2_out, not_3_out, D, E, not_7_out);
  and and_124 (and_124_out, not_1_out, not_3_out, D, E, G);
  and and_125 (and_125_out, not_1_out, not_2_out, not_3_out, D, G);
  and and_126 (and_126_out, not_1_out, B, not_3_out, D, E, not_6_out, G);
  and and_127 (and_127_out, not_1_out, B, C, D, E, F, not_7_out);
  and and_128 (and_128_out, not_1_out, B, C, not_4_out, E, F, G);
  and and_129 (and_129_out, not_1_out, B, C, D, not_6_out, G);
  and and_130 (and_130_out, not_1_out, B, C, D, not_5_out, not_6_out);
  and and_131 (and_131_out, not_1_out, B, C, not_4_out, E, not_6_out, G);
  and and_132 (and_132_out, not_1_out, B, C, not_4_out, E, F, not_7_out);
  and and_133 (and_133_out, not_1_out, B, C, D, not_5_out, not_6_out);
  and and_134 (and_134_out, not_1_out, B, C, D, not_5_out, not_6_out, G);
  and and_135 (and_135_out, not_1_out, B, C, not_4_out, E, not_7_out);
  and and_136 (and_136_out, not_1_out, B, C, not_4_out, E, F);
  and and_137 (and_137_out, not_1_out, B, not_3_out, D, E, not_6_out, not_7_out);
  and and_138 (and_138_out, not_1_out, B, C, not_4_out, not_5_out, F, not_7_out);
  and and_139 (and_139_out, A, not_2_out, not_3_out, not_4_out, not_5_out, F);
  and and_140 (and_140_out, not_2_out, not_3_out, not_4_out, not_5_out, not_6_out, G);
  and and_141 (and_141_out, not_1_out, B, not_3_out, D, E, not_6_out, not_7_out);
  and and_142 (and_142_out, not_1_out, B, not_3_out, D, E, F, G);
  and and_143 (and_143_out, not_1_out, B, C, not_4_out, not_5_out, not_7_out);
  and and_144 (and_144_out, not_1_out, B, not_3_out, D, not_5_out, F, G);
  and and_145 (and_145_out, not_1_out, B, not_3_out, D, E, not_6_out, G);
  and and_146 (and_146_out, not_1_out, B, not_3_out, D, E, F, not_7_out);
  and and_147 (and_147_out, not_1_out, B, C, not_4_out, not_5_out, not_6_out, G);
  and and_148 (and_148_out, not_1_out, B, C, D, E, not_6_out, not_7_out);
  and and_149 (and_149_out, A, not_2_out, not_3_out, not_4_out, E, not_6_out, not_7_out);
  and and_150 (and_150_out, A, not_2_out, C, not_4_out, not_5_out, not_6_out, not_7_out);
  and and_151 (and_151_out, not_1_out, B, C, D, not_5_out, F);
  and and_152 (and_152_out, A, not_2_out, not_3_out, not_4_out, not_5_out, not_6_out, not_7_out);
  and and_153 (and_153_out, not_1_out, B, C, D, E, F);
  and and_154 (and_154_out, A, not_2_out, not_3_out, not_4_out, not_5_out, G);
  and and_155 (and_155_out, A, not_2_out, not_3_out, not_4_out, not_5_out, F);
  and and_156 (stPC, not_1_out, B, C, D, not_5_out, F, not_7_out);
  and and_157 (Reti, A, not_2_out, not_3_out, not_4_out, E, not_6_out, not_7_out);
  and and_158 (randomSel, A, not_2_out, not_3_out, not_4_out, E, F, G);
  and and_159 (read_flags, A, not_2_out, not_3_out, D, not_5_out, not_6_out, not_7_out);
  and and_160 (storeFlagI, A, not_2_out, not_3_out, D, not_5_out, not_6_out, G);
  or or_1 (iem1, and_126_out, and_127_out);
  or or_2 (br0, and_128_out, and_129_out, and_130_out);
  or or_3 (br1, and_131_out, and_132_out, and_133_out);
  or or_4 (br2, and_134_out, and_135_out, and_136_out);
  or or_5 (ld, and_141_out, and_142_out, and_143_out);
  or or_6 (ioW, and_152_out, and_153_out);
  or or_7 (ioR, and_154_out, and_155_out);
  or or_8 (aluop0, and_42_out, and_43_out, and_44_out, and_45_out, and_46_out, and_47_out, and_48_out);
  or or_9 (aluop2, and_49_out, and_50_out, and_51_out, and_52_out, and_53_out, and_54_out, and_55_out);
  or or_10 (aluop3, and_56_out, and_57_out, and_58_out, and_59_out, and_60_out, and_61_out, and_62_out, and_63_out, and_64_out);
  or or_11 (aluop4, and_65_out, and_66_out, and_67_out, and_68_out, and_69_out, and_70_out, and_71_out, and_72_out, and_73_out);
  or or_12 (sf, and_104_out, and_105_out, and_106_out, and_107_out, and_108_out, and_109_out, and_110_out, and_111_out, and_112_out, and_113_out);
  or or_13 (muxA, and_137_out, and_138_out, and_139_out, and_140_out);
  or or_14 (st, and_144_out, and_145_out, and_146_out, and_147_out);
  or or_15 (abs, and_148_out, and_149_out, and_150_out, and_151_out);
  or or_16 (muxb0, and_1_out, and_2_out, and_3_out, and_4_out, and_5_out, and_6_out, and_7_out, and_8_out, and_9_out, and_10_out, and_11_out, and_12_out, and_13_out, and_14_out);
  or or_17 (muxb1, and_15_out, and_16_out, and_17_out, and_18_out, and_19_out, and_20_out, and_21_out, and_22_out, and_23_out, and_24_out, and_25_out, and_26_out, and_27_out, and_28_out);
  or or_18 (muxb2, and_29_out, and_30_out, and_31_out, and_32_out, and_33_out, and_34_out, and_35_out, and_36_out, and_37_out, and_38_out, and_39_out, and_40_out, and_41_out);
  or or_19 (aluop5, and_74_out, and_75_out, and_76_out, and_77_out, and_78_out, and_79_out, and_80_out, and_81_out, and_82_out, and_83_out, and_84_out, and_85_out, and_86_out, and_87_out, and_88_out);
  or or_20 (WE, and_89_out, and_90_out, and_91_out, and_92_out, and_93_out, and_94_out, and_95_out, and_96_out, and_97_out, and_98_out, and_99_out, and_100_out, and_101_out, and_102_out, and_103_out);
  or or_21 (iem0, and_114_out, and_115_out, and_116_out, and_117_out, and_118_out, and_119_out, and_120_out, and_121_out, and_122_out, and_123_out, and_124_out, and_125_out);

  assign aluop1 = 1'b0;
  assign timerSel = 1'b0;
endmodule
