// Digital circuit lfsr RandomNumberGen.dig as structural Verilog
module lfsr_RandomNumberGen (
  input  [15:0] adrrIn,
  input  [15:0] dataIn,
  input  ioW,
  input  clk,
  input  [15:0] SeedAdr,
  output [15:0] Out
);

  wire and_1_out, and_2_out, and_3_out, comparator_1_eq, d_ff_as_1_nq, d_ff_as_1_q, jk_ff_1_q, not_1_out,
       or_1_out, xor_1_out, xor_2_out, xor_3_out;
  wire [15:0] multiplexer_1_out, seed_q;

  Comparator #(.Signed("true"), .Bits(16)) comparator_1 (
    .a(adrrIn), .b(SeedAdr), .eq(comparator_1_eq));  // open: gt, lt
  and and_1 (and_1_out, comparator_1_eq, ioW);
  not not_1 (not_1_out, or_1_out);
  and and_2 (and_2_out, clk, and_1_out);
  and and_3 (and_3_out, and_1_out, not_1_out);
  JK_FF jk_ff_1 (.J(or_1_out), .C(clk), .K(or_1_out), .Q(jk_ff_1_q));  // open: nQ
  D_FF_AS d_ff_as_1 (.Set(1'b0), .D(d_ff_as_1_nq), .C(and_2_out), .Clr(jk_ff_1_q), .Q(d_ff_as_1_q), .nQ(d_ff_as_1_nq));
  Register #(.Bits(16)) seed (.D(dataIn), .C(clk), .en(and_1_out), .Q(seed_q));
  or or_1 (or_1_out, d_ff_as_1_q, jk_ff_1_q);
  Multiplexer #(.Bits(16)) multiplexer_1 (.sel(and_1_out), .in_0({16{1'b0}}), .in_1(seed_q), .out(multiplexer_1_out));
  // Probe on Out
  D_FF_AS d_ff_as_2 (.Set(multiplexer_1_out[0]), .D(xor_1_out), .C(clk), .Clr(and_3_out), .Q(Out[0]));  // open: nQ
  D_FF_AS d_ff_as_3 (.Set(multiplexer_1_out[1]), .D(Out[0]), .C(clk), .Clr(and_3_out), .Q(Out[1]));  // open: nQ
  D_FF_AS d_ff_as_4 (.Set(multiplexer_1_out[2]), .D(Out[1]), .C(clk), .Clr(and_3_out), .Q(Out[2]));  // open: nQ
  D_FF_AS d_ff_as_5 (.Set(multiplexer_1_out[3]), .D(Out[2]), .C(clk), .Clr(and_3_out), .Q(Out[3]));  // open: nQ
  D_FF_AS d_ff_as_6 (.Set(multiplexer_1_out[4]), .D(Out[3]), .C(clk), .Clr(and_3_out), .Q(Out[4]));  // open: nQ
  D_FF_AS d_ff_as_7 (.Set(multiplexer_1_out[5]), .D(Out[4]), .C(clk), .Clr(and_3_out), .Q(Out[5]));  // open: nQ
  D_FF_AS d_ff_as_8 (.Set(multiplexer_1_out[6]), .D(Out[5]), .C(clk), .Clr(and_3_out), .Q(Out[6]));  // open: nQ
  D_FF_AS d_ff_as_9 (.Set(multiplexer_1_out[7]), .D(Out[6]), .C(clk), .Clr(and_3_out), .Q(Out[7]));  // open: nQ
  D_FF_AS d_ff_as_10 (.Set(multiplexer_1_out[8]), .D(Out[7]), .C(clk), .Clr(and_3_out), .Q(Out[8]));  // open: nQ
  D_FF_AS d_ff_as_11 (.Set(multiplexer_1_out[9]), .D(Out[8]), .C(clk), .Clr(and_3_out), .Q(Out[9]));  // open: nQ
  D_FF_AS d_ff_as_12 (.Set(multiplexer_1_out[10]), .D(Out[9]), .C(clk), .Clr(and_3_out), .Q(Out[10]));  // open: nQ
  xor xor_1 (xor_1_out, xor_2_out, Out[10]);
  D_FF_AS d_ff_as_13 (.Set(multiplexer_1_out[11]), .D(Out[10]), .C(clk), .Clr(and_3_out), .Q(Out[11]));  // open: nQ
  D_FF_AS d_ff_as_14 (.Set(multiplexer_1_out[12]), .D(Out[11]), .C(clk), .Clr(and_3_out), .Q(Out[12]));  // open: nQ
  xor xor_2 (xor_2_out, xor_3_out, Out[12]);
  xor xor_3 (xor_3_out, Out[13], Out[15]);
  D_FF_AS d_ff_as_15 (.Set(multiplexer_1_out[13]), .D(Out[12]), .C(clk), .Clr(and_3_out), .Q(Out[13]));  // open: nQ
  D_FF_AS d_ff_as_16 (.Set(multiplexer_1_out[14]), .D(Out[13]), .C(clk), .Clr(and_3_out), .Q(Out[14]));  // open: nQ
  D_FF_AS d_ff_as_17 (.Set(multiplexer_1_out[15]), .D(Out[14]), .C(clk), .Clr(and_3_out), .Q(Out[15]));  // open: nQ

  // Other names for the same wires on the sheet: RandomNUM[15:0] = Out; AddrOut[15:0] = adrrIn; Clk_in = clk;
  //   DataOut[15:0] = dataIn; RandomSeedReg[15:0] = SeedAdr

  // Notes on the sheet:
  //   RandomNumberGen
endmodule
