// Digital circuit 1-addressable register.dig as structural Verilog
module _1_addressable_register (
  input  [15:0] Datain,
  input  ioW,
  input  [15:0] addrIn,
  input  [15:0] address,
  input  clk,
  output DataOut
);

  wire and_1_out, comparator_1_eq;

  Comparator #(.Bits(16)) comparator_1 (.a(addrIn), .b(address), .eq(comparator_1_eq));  // open: gt, lt
  and and_1 (and_1_out, comparator_1_eq, ioW);
  Register addrReg (.D(Datain[0]), .C(clk), .en(and_1_out), .Q(DataOut));

  // Other names for the same wires on the sheet: C = clk; DataIn_t = Datain[0]
endmodule
