// Digital circuit fpu.dig as structural Verilog
module fpu (
  input  clk,
  input  in_2,
  input  in_3,
  input  [15:0] in_4,
  input  [15:0] in_5,
  input  [1:0] in_6,
  output [15:0] out_7
);

  wire u_fpu16_busy, u_fpu16_done;

  fpu16 #(.applicationType("IVERILOG"), .CodeFile("D:\\Desktop\\fpga\\RemedyCpu\\verilog\\fpu16.v")) u_fpu16 (
    .clk(clk), .rst(in_2), .start(in_3), .op(in_6), .a(in_5), .b(in_4), .result(out_7), .busy(u_fpu16_busy),
    .done(u_fpu16_done));
endmodule
