// Digital circuit newDesign.dig as structural Verilog
module newDesign (
  input  [7:0] Input,
  input  rst_n,
  input  spiMiso,
  input  RX,
  input  clk_internal,
  output [3:0] debugOut,
  output spiClk,
  output spiMosi,
  output spiCSRam,
  output [7:0] Output,
  output TX,
  output spiCSProg,
  output [5:0] spiDeb
);

  wire _1_addressable_register_1_dataout, abs, and_1_out, and_2_out, and_3_out, and_4_out, and_5_out,
       and_7_out, and_8_out, and_12_out, comparator_1_eq, comparator_2_eq, comparator_3_eq, comparator_4_gt,
       comparator_4_lt, comparator_5_eq, comparator_6_eq, comparator_7_gt, comparator_7_lt, counter_1_ovf,
       d_ff_q, demultiplexer_1_out_0, demultiplexer_1_out_1, dipswitch_1_out, Exevute, inputEn, instDecode,
       instFetch, instRead, inter, interEn, interEnable, InterLock, intr, ioR, ioW, ld, multiplexer_6_out,
       multiplexer_8_out, multiplexer_9_out, multiplexer_10_out, muxA, nor_1_out, nor_2_out, or_4_out,
       or_5_out, or_6_out, or_7_out, or_8_out, or_9_out, or_13_out, or_14_out, RandomNUMSel, read_the_flags,
       Reti, rst, sf, spi_busy_ram, SpiRam_spi_clk, SpiRam_spi_mosi, st, store_the_flags, stPC, timer0En,
       timer1En, timer2En, undriven, undriven_2, undriven_3, WE, xor_1_out;
  wire [1:0] iem;
  wire [2:0] br, FlagOut, muxB, or_3_out, or_10_out;
  wire [3:0] and_11_out;
  wire [4:0] aluOp;
  wire [6:0] multiplexer_1_out;
  wire [7:0] outputToOutsideEnable;
  wire [15:0] AddrOut, CurrentOpcode, DataOut, din_bus, imreg_1_p5, inputReg, Instruction_q, interruptReg,
       iow_Din, multiplexer_2_out, multiplexer_3_out, multiplexer_7_out, multiplexer_11_out,
       multiplexer_12_out, multiplexer_14_out, multiplexer_15_out, multiplexer_16_out, pgr_d, programAddr,
       programOpcode, RandomNUM, register_1_q, register_2_q, registerblock_1_rdest, singextend_1__4d,
       singextend_1__4s, singextend_1__8sd, SpiRam_data_out, time0In, time1In, time2In,
       u_programCounter_nextpc;
  wire [17:0] counter_1_out;

  _1_addressable_register intEn (
    .Datain(DataOut), .ioW(ioW), .addrIn(AddrOut), .address(16'ha), .clk(spiDeb[0]), .DataOut(interEnable));
  not not_1 (rst, rst_n);
  not not_2 (spiCSProg, demultiplexer_1_out_1);
  not not_3 (spiCSRam, demultiplexer_1_out_0);
  Demultiplexer demultiplexer_1 (
    .sel(instRead), .in(spi_busy_ram), .out_0(demultiplexer_1_out_0), .out_1(demultiplexer_1_out_1));
  and and_1 (and_1_out, intr, interEnable);
  and and_2 (and_2_out, interEnable, Reti);
  Counter #(.Bits(19)) counter_1 (
    .en(1'b1), .C(clk_internal), .clr(counter_1_ovf), .out({spiDeb[0], counter_1_out}), .ovf(counter_1_ovf));
  programCounter #(.applicationType("IVERILOG"), .CodeFile("C:\\Users\\Berkant\\Desktop\\fpga\\RemedyCpu\\verilog\\programCounter.v")) u_programCounter (
    .AluIn(AddrOut), .clk(debugOut[3]), .rst(rst), .absJmp(abs), .intr(and_1_out), .reti(and_2_out),
    .relJmp(xor_1_out), .Nextpc(u_programCounter_nextpc), .PC(programAddr));
  ClockCont #(.applicationType("IVERILOG"), .CodeFile("D:\\Desktop\\fpga\\RemedyCpu\\verilog\\clockController.v")) u_ClockCont (
    .Clk(spiDeb[0]), .Enable(spi_busy_ram), .rst(rst), .instRead(instRead), .instFetch(instFetch),
    .instDecode(instDecode), .instExecute(Exevute));
  Multiplexer #(.Bits(7)) multiplexer_1 (
    .sel(CurrentOpcode[15]), .in_0(CurrentOpcode[14:8]), .in_1({7{1'b0}}), .out(multiplexer_1_out));
  // controllogic controllogic_1: pin names not known; wires that end beside it: multiplexer_1_out[6], multiplexer_1_out[5], multiplexer_1_out[4], multiplexer_1_out[3], multiplexer_1_out[2], multiplexer_1_out[1], multiplexer_1_out[0], muxB[2], muxB[1], muxB[0], aluOp[4], aluOp[3], aluOp[2], aluOp[1], aluOp[0], WE, sf, iem[1], iem[0], br[2], br[1], br[0], muxA, ld, st, abs, ioW, ioR, stPC, Reti, RandomNUMSel
  ROM #(.AddrBits(16), .isProgramMemory("true"), .Bits(16)) pgr (.A(programAddr), .sel(1'b1), .D(pgr_d));
  or or_1 (or_3_out[2], 1'b0, RandomNUMSel, read_the_flags);
  Multiplexer #(.Selector_Bits(3), .Bits(16)) multiplexer_2 (
    .sel(or_3_out), .in_0(AddrOut), .in_1(din_bus), .in_2(iow_Din), .in_3(u_programCounter_nextpc),
    .in_4({16{1'b0}}), .in_5(RandomNUM), .in_6({{13{1'b0}}, FlagOut}), .in_7({16{1'b0}}),
    .out(multiplexer_2_out));
  Register #(.Bits(16)) Instruction (.D(programOpcode), .C(instFetch), .en(1'b1), .Q(Instruction_q));
  or or_2 (or_3_out[1], ioR, stPC, read_the_flags);
  Multiplexer #(.Bits(16)) multiplexer_3 (
    .sel(dipswitch_1_out), .in_0(Instruction_q), .in_1(pgr_d), .out(multiplexer_3_out));
  DipSwitch dipswitch_1 (.out(dipswitch_1_out));
  Multiplexer multiplexer_4 (.sel(dipswitch_1_out), .in_0(Exevute), .in_1(spiDeb[0]), .out(debugOut[3]));
  or or_3 (or_3_out[0], ld, stPC, RandomNUMSel);
  Multiplexer #(.Bits(16)) multiplexer_5 (
    .sel(instDecode), .in_0({16{1'b0}}), .in_1(multiplexer_3_out), .out(CurrentOpcode));
  xor xor_1 (xor_1_out, multiplexer_6_out, br[2]);
  Multiplexer #(.Selector_Bits(2)) multiplexer_6 (
    .sel(br[1:0]), .in_0(1'b0), .in_1(FlagOut[0]), .in_2(FlagOut[1]), .in_3(FlagOut[2]),
    .out(multiplexer_6_out));
  Multiplexer #(.Bits(16)) multiplexer_7 (
    .sel(instRead), .in_0({AddrOut[14:0], 1'b0}), .in_1({programAddr[14:0], 1'b0}), .out(multiplexer_7_out));
  or or_4 (or_4_out, st, st);
  or or_5 (or_5_out, ld, instRead);
  register_1bit NegR (.D(multiplexer_8_out), .C(spiDeb[0]), .en(sf), .rst(rst), .Q(FlagOut[2]));
  register_1bit ZeroR (.D(multiplexer_9_out), .C(spiDeb[0]), .en(sf), .rst(rst), .Q(FlagOut[1]));
  register_1bit CarryR (.D(multiplexer_10_out), .C(spiDeb[0]), .en(sf), .rst(rst), .Q(FlagOut[0]));
  RegisterBlock registerblock_1 (
    .DataIn(multiplexer_2_out), .WE(WE), .clk(debugOut[3]), .src(CurrentOpcode[3:0]),
    .Dest(CurrentOpcode[7:4]), .rst(rst), .RDest(registerblock_1_rdest), .Rsrc(DataOut));
  // ImReg imreg_1: pin names not known; wires that end beside it: CurrentOpcode[15], iem, debugOut[3], CurrentOpcode, imreg_1_p5
  singExtend singextend_1 (
    .inst(CurrentOpcode), ._4S(singextend_1__4s), ._8SD(singextend_1__8sd), ._4D(singextend_1__4d));
  nor nor_1 (nor_1_out, or_4_out, or_5_out);
  and and_3 (and_3_out, InterLock, ~Reti);  // And
  and and_4 (and_4_out, d_ff_q, ~Reti);  // And
  and and_5 (and_5_out, inter, interEnable);
  or or_6 (or_6_out, rst, nor_1_out);
  or or_7 (or_7_out, and_3_out, intr);
  or or_8 (or_8_out, and_4_out, and_5_out);
  Multiplexer multiplexer_8 (
    .sel(store_the_flags), .in_0(undriven), .in_1(multiplexer_11_out[2]), .out(multiplexer_8_out));
  Multiplexer multiplexer_9 (
    .sel(store_the_flags), .in_0(undriven_2), .in_1(multiplexer_11_out[1]), .out(multiplexer_9_out));
  Multiplexer multiplexer_10 (
    .sel(store_the_flags), .in_0(undriven_3), .in_1(multiplexer_11_out[0]), .out(multiplexer_10_out));
  D_FF d_ff (.D(or_8_out), .C(~spiDeb[0]), .Q(d_ff_q));  // open: nQ
  Multiplexer #(.Bits(16)) multiplexer_11 (
    .sel(muxA), .in_0(registerblock_1_rdest), .in_1(DataOut), .out(multiplexer_11_out));
  Multiplexer #(.Selector_Bits(3), .Bits(16)) multiplexer_12 (
    .sel(muxB), .in_0(DataOut), .in_1({16{1'b0}}), .in_2(imreg_1_p5), .in_3({16{1'b0}}), .in_4({16{1'b0}}),
    .in_5(singextend_1__4s), .in_6(singextend_1__8sd), .in_7(singextend_1__4d), .out(multiplexer_12_out));
  spiden SpiRam (
    .spi_miso(spiMiso), .Address(multiplexer_7_out), .clk(spiDeb[0]), .st(or_4_out), .DataIn(DataOut),
    .ld(or_5_out), .spi_rst(or_6_out), .spi_clk(SpiRam_spi_clk), .spi_mosi(SpiRam_spi_mosi),
    .Busy(spi_busy_ram), .data_out(SpiRam_data_out));
  D_FF d_ff_2 (.D(or_7_out), .C(~spiDeb[0]), .Q(InterLock));  // open: nQ
  assign spiClk = spi_busy_ram ? SpiRam_spi_clk : 1'bz;  // Driver driver_1
  and and_6 (intr, ~InterLock, ~CurrentOpcode[15], d_ff_q, ~1'b0);  // And
  assign spiDeb[2] = spi_busy_ram ? SpiRam_spi_mosi : 1'bz;  // Driver driver_2
  Demultiplexer #(.Bits(16)) demultiplexer_2 (
    .sel(nor_2_out), .in(SpiRam_data_out), .out_0(din_bus), .out_1(programOpcode));
  nor nor_2 (nor_2_out, st, ld);
  Alu alu_1 (
    .A(multiplexer_11_out), .B(multiplexer_12_out), .carryIn(FlagOut[0]), .AluOp(aluOp));  // open: Out, Neg, Zero, CarryOut
  lfsr_RandomNumberGen lfsr_randomnumbergen_1 (
    .adrrIn(AddrOut), .dataIn(DataOut), .ioW(ioW), .clk(debugOut[3]), .SeedAdr(16'hd), .Out(RandomNUM));
  timer timer0 (
    .dOut(DataOut), .Addr(AddrOut), .ioW(ioW), .ioR(ioR), .C(debugOut[3]), .InterLock(InterLock),
    .timerConfigAddr(16'h1), .timerTargetAddr(16'h2), .timerResetAddr(16'h3), .timerReadAddr(16'h1),
    .rst(rst), .TimerOut(time0In), .\timerİnterrupt (and_11_out[0]), .TimerEn(timer0En));
  timer timer1 (
    .dOut(DataOut), .Addr(AddrOut), .ioW(ioW), .ioR(ioR), .C(debugOut[3]), .InterLock(InterLock),
    .timerConfigAddr(16'h4), .timerTargetAddr(16'h5), .timerResetAddr(16'h6), .timerReadAddr(16'h2),
    .rst(rst), .TimerOut(time1In), .\timerİnterrupt (and_11_out[1]), .TimerEn(timer1En));
  timer timer2 (
    .dOut(DataOut), .Addr(AddrOut), .ioW(ioW), .ioR(ioR), .C(debugOut[3]), .InterLock(InterLock),
    .timerConfigAddr(16'h7), .timerTargetAddr(16'h8), .timerResetAddr(16'h9), .timerReadAddr(16'h3),
    .rst(rst), .TimerOut(time2In), .\timerİnterrupt (and_11_out[2]), .TimerEn(timer2En));
  Comparator #(.Signed("true"), .Bits(16)) comparator_1 (.a(AddrOut), .b(16'hc), .eq(comparator_1_eq));  // open: gt, lt
  Comparator #(.Signed("true"), .Bits(16)) comparator_2 (.a(AddrOut), .b(16'hb), .eq(comparator_2_eq));  // open: gt, lt
  Comparator #(.Signed("true"), .Bits(16)) comparator_3 (.a(AddrOut), .b(16'hb), .eq(comparator_3_eq));  // open: gt, lt
  and and_7 (and_7_out, comparator_1_eq, ioW);
  and and_8 (and_8_out, comparator_2_eq, ioW);
  and and_9 (inputEn, comparator_3_eq, ioR);
  _1_addressable_register _1_addressable_register_1 (
    .Datain(DataOut), .ioW(ioW), .addrIn(AddrOut), .address(16'he), .clk(debugOut[3]),
    .DataOut(_1_addressable_register_1_dataout));
  Multiplexer #(.Selector_Bits(3), .Bits(16)) multiplexer_13 (
    .sel(or_10_out), .in_0({16{1'b0}}), .in_1(interruptReg), .in_2(inputReg), .in_3(time0In), .in_4(time1In),
    .in_5(time2In), .in_6({16{1'b0}}), .in_7({16{1'b0}}), .out(iow_Din));
  register_8bit outputReg (.D(DataOut[7:0]), .C(debugOut[3]), .en(and_7_out), .rst(rst), .Q(outputToOutsideEnable));
  Multiplexer #(.Bits(16)) multiplexer_14 (
    .sel(InterLock), .in_0({{8{1'b0}}, Input}), .in_1(register_1_q), .out(multiplexer_14_out));
  Register #(.Bits(16)) register_1 (.D(multiplexer_14_out), .C(debugOut[3]), .en(or_9_out), .Q(register_1_q));
  uartBlock uartblock_1 (
    .TX(TX), .RX(RX), .clk(debugOut[3]), .localclk(spiDeb[0]), .rst(rst), .dataIn(DataOut), .Addr(AddrOut),
    .ioW(ioW), .ioR(ioR), .transmitAddr(16'h10), .ReceiveAddr(16'h5));  // open: DataOut
  register_8bit OutoutEnReg (.D(DataOut[7:0]), .C(debugOut[3]), .en(and_8_out), .rst(rst), .Q(Output));
  Comparator #(.Bits(16)) comparator_4 (
    .a(multiplexer_14_out), .b(register_1_q), .gt(comparator_4_gt), .lt(comparator_4_lt));  // open: eq
  Comparator #(.Bits(16)) comparator_5 (.a(16'h4), .b(AddrOut), .eq(comparator_5_eq));  // open: gt, lt
  or or_9 (or_9_out, comparator_4_gt, comparator_4_lt);
  or or_10 (or_10_out[2], timer1En, timer2En, 1'b0);
  or or_11 (or_10_out[1], inputEn, timer0En, 1'b0);
  or or_12 (or_10_out[0], interEn, timer0En, timer2En);
  Comparator #(.Bits(16)) comparator_6 (.a(16'ha), .b(AddrOut), .eq(comparator_6_eq));  // open: gt, lt
  and and_10 (interEn, comparator_5_eq, ioR);
  and and_11 (and_11_out[3], or_9_out, _1_addressable_register_1_dataout);
  Multiplexer #(.Bits(16)) multiplexer_15 (
    .sel(and_12_out), .in_0({{12{1'b0}}, and_11_out}), .in_1(DataOut), .out(multiplexer_15_out));
  and and_12 (and_12_out, comparator_6_eq, ioW);
  Register #(.Bits(16)) register_2 (.D(multiplexer_15_out), .C(debugOut[3]), .en(or_13_out), .Q(register_2_q));
  Multiplexer #(.Bits(16)) multiplexer_16 (
    .sel(_1_addressable_register_1_dataout), .in_0({{8{1'b0}}, Input}), .in_1(register_1_q),
    .out(multiplexer_16_out));
  assign inputReg = inputEn ? multiplexer_16_out : 16'bz;  // Driver driver_3
  Comparator #(.Bits(16)) comparator_7 (
    .a(multiplexer_15_out), .b(register_2_q), .gt(comparator_7_gt), .lt(comparator_7_lt));  // open: eq
  assign interruptReg = interEn ? register_2_q : 16'bz;  // Driver driver_4
  or or_13 (or_13_out, comparator_7_gt, comparator_7_lt);
  and and_13 (inter, ~InterLock, or_14_out);  // And
  or or_14 (or_14_out, 1'b0, 1'b0, 1'b0, 1'b0, 1'b0, 1'b0, 1'b0, 1'b0, 1'b0, 1'b0, 1'b0, 1'b0, and_11_out[3], and_11_out[2], and_11_out[1], and_11_out[0]);

  assign debugOut[2:0] = {3{debugOut[3]}};
  assign {spiDeb[5:3], spiDeb[1]} = {spiCSRam, spiCSProg, spiClk, spiMiso};
  assign spiMosi = spiDeb[2];

  // Other names for the same wires on the sheet: Clk_in = spiDeb[0]; PeripheralClk_in = spiDeb[0];
  //   OPcode[7:0] = CurrentOpcode[15:8]; imm = CurrentOpcode[15]; inputFromOutside[7:0] = Input;
  //   outputToOutside[7:0] = Output; pcClock = debugOut[3]; spi_clock_ram = spiClk; spi_miso = spiMiso;
  //   spi_mosi_ram = spiDeb[2]; uart_rx = RX; uart_tx = TX

  // Notes on the sheet:
  //   rst_n: default 1
  //   clk_internal: Hz: 4000000
  //   Input/Output
  //   ControlLogic
  //   MainClockController
  //   pgr loads int.hex
  //   JumpLogic
  //   FlagStore
  //   ProgramMemoryRead
  //   IO Addresses
  //   interrupt Logic
  //   Write Addresses
  //   Read Addresses
  //   RandomNumberGen
  //   IO BUS
  //   Timers
  //   Output
  //   Output_En
  //   input
  //   inputBus
  //   InterruptRegister
  //   InterruptBus
endmodule
