// Digital circuit tt_um_remedy_cpu_qspi_simulation.dig as structural Verilog
module tt_um_remedy_cpu_qspi_simulation (
  input  [7:0] ui_in,
  input  clk,
  input  ena,
  input  rst_n,
  input  [3:0] in_7,
  input  [15:0] in_8,
  output [7:0] uo_out,
  output [7:0] IO_bidir
);

  wire abs, and_1_out, and_2_out, and_3_out, and_4_out, and_5_out, and_9_out, and_10_out, and_11_out,
       and_12_out, and_13_out, and_15_out, and_16_out, and_18_out, and_19_out, and_20_out, and_21_out,
       and_22_out, and_23_out, and_24_out, and_25_out, and_26_out, Break, bussplitter_2_d, button_1_out,
       button_2_out, button_3_out, button_4_out, button_5_out, button_6_out, button_7_out, button_8_out,
       Clk_in, comparator_1_eq, data_done, dbg_clk, dbg_data_in, dbg_data_oe, dbg_data_out, dbg_en,
       dbg_halted, deb_jump_req, dipswitch_1_out, dipswitch_2_out, driver_1_out, execute_pulse, Fetch_done,
       fetch_request_pulse, flash_req, halt_req, i2c_inter, imm, InterLock, intr, ioR, ioW, ld,
       multiplexer_6_out, muxA, not_1_out, not_2_out, not_3_out, not_4_out, not_5_out, not_6_out, not_7_out,
       not_8_out, not_9_out, or_1_out, or_2_out, or_4_out, pc_en, Reti, rst_complex, run_req, scl_o, scl_oe,
       sf, soft_reset_req, spi_busy_ram, spi_ld, spi_st, spi_target, st, step_req, stPC, ststic_break_en,
       u_Alu_carryout, u_Alu_neg, u_Alu_zero, u_debug_core_tiny_dbg_break_after_exec,
       u_debug_core_tiny_dbg_break_hit, u_debug_panel_serial_sim_tiny_busy,
       u_debug_panel_serial_sim_tiny_dbg_data_oe, u_debug_panel_serial_sim_tiny_dbg_data_out,
       u_debug_panel_serial_sim_tiny_dbg_enable_state,
       u_debug_panel_serial_sim_tiny_static_break_enable_state, u_debug_serial_frontend_tiny_reg_wr,
       u_memory_wait_controller_tiny_mem_stall, u_opcode_microcode_rom_ior, u_opcode_microcode_rom_iow,
       u_opcode_microcode_rom_sf, u_opcode_microcode_rom_we, WE, xor_1_out;
  wire [1:0] iem, u_muxEncoder_q, u_timer_tiny_timer_interrupt;
  wire [2:0] br, flag_out, muxB, or_7_out;
  wire [3:0] u_debug_serial_frontend_tiny_reg_addr;
  wire [5:0] aluOp;
  wire [6:0] multiplexer_1_out;
  wire [7:0] IO_in, IO_out;
  wire [7:1] IO_oe;
  wire [7:6] outputToOutside;
  wire [14:0] inst_reg;
  wire [15:0] add_1_s, AddrOut, DataOut, deb_jump_addr, i2cDat, ImmReg, intr_reg, iow_Din, mem_out,
       multiplexer_5_out, multiplexer_7_out, multiplexer_8_out, programAddr, reg_rdata, rngdat0,
       singextend_1_p2, singextend_1_p3, singextend_1_p4, spi_addr, spi_data, spi_data_out, timerdat1,
       timerdat2, u_debug_panel_serial_sim_tiny_last_response, u_debug_panel_serial_sim_tiny_live_rdata,
       u_debug_serial_frontend_tiny_reg_wdata, u_RegisterBlock_rdest;

  Button button_1 (.out(button_1_out));
  Button button_2 (.out(button_2_out));
  Button button_3 (.out(button_3_out));
  Button button_4 (.out(button_4_out));
  DipSwitch dipswitch_1 (.out(dipswitch_1_out));
  DipSwitch dipswitch_2 (.out(dipswitch_2_out));
  Button button_5 (.out(button_5_out));
  Button button_6 (.out(button_6_out));
  Button button_7 (.out(button_7_out));
  Button button_8 (.out(button_8_out));
  debug_panel_serial_sim_tiny #(.applicationType("IVERILOG"), .CodeFile("D:\\Desktop\\fpga\\RemedyCpu\\verilog\\debug_panel_serial_sim_tiny_newdbg_controls.v")) u_debug_panel_serial_sim_tiny (
    .clk(Clk_in), .rst_n(rst_n), .btn_dbg_toggle(dipswitch_1_out), .btn_static_break_toggle(dipswitch_2_out),
    .btn_halt(button_5_out), .btn_run(button_1_out), .btn_step(button_6_out), .btn_soft_reset(button_2_out),
    .btn_jump(button_7_out), .btn_write(button_3_out), .btn_read(button_8_out), .btn_ping(button_4_out),
    .sw_addr(in_7), .sw_wdata(in_8), .dbg_data_in(dbg_data_in), .dbg_clk(dbg_clk),
    .dbg_data_out(u_debug_panel_serial_sim_tiny_dbg_data_out),
    .dbg_data_oe(u_debug_panel_serial_sim_tiny_dbg_data_oe),
    .live_rdata(u_debug_panel_serial_sim_tiny_live_rdata),
    .last_response(u_debug_panel_serial_sim_tiny_last_response), .busy(u_debug_panel_serial_sim_tiny_busy),
    .dbg_enable_state(u_debug_panel_serial_sim_tiny_dbg_enable_state),
    .static_break_enable_state(u_debug_panel_serial_sim_tiny_static_break_enable_state));
  // Probe debug_data on dbg_data_in
  assign driver_1_out = u_debug_panel_serial_sim_tiny_dbg_data_oe ? u_debug_panel_serial_sim_tiny_dbg_data_out : 1'bz;  // Driver driver_1
  BusSplitter bussplitter_1 (.D(driver_1_out), .OE(u_debug_panel_serial_sim_tiny_dbg_data_oe), .D0(dbg_data_in));
  BusSplitter bussplitter_2 (.D(bussplitter_2_d), .OE(dbg_data_oe), .D0(dbg_data_in));
  assign bussplitter_2_d = dbg_data_oe ? dbg_data_out : 1'bz;  // Driver driver_2
  bidir_wrapper #(.applicationType("IVERILOG"), .CodeFile("D:\\Desktop\\fpga\\RemedyCpu\\verilog\\bidir_wrapper.v")) u_bidir_wrapper (
    .data_out(IO_out), .data_oe({IO_oe[7], 1'b1, IO_oe[5:4], 1'b1, IO_oe[2:1], 1'b1}), .data_in(IO_in),
    .io(IO_bidir));
  and and_1 (and_1_out, intr, execute_pulse);
  and and_2 (and_2_out, execute_pulse, Reti);
  and and_3 (and_3_out, abs, execute_pulse);
  not not_1 (not_1_out, soft_reset_req);
  Multiplexer #(.Bits(7)) multiplexer_1 (.sel(imm), .in_0(inst_reg[14:8]), .in_1({7{1'b0}}), .out(multiplexer_1_out));
  Multiplexer multiplexer_2 (.sel(scl_oe), .in_0(outputToOutside[6]), .in_1(scl_o), .out(uo_out[6]));
  Multiplexer multiplexer_3 (.sel(dbg_data_oe), .in_0(outputToOutside[7]), .in_1(outputToOutside[7]), .out(uo_out[7]));
  Multiplexer multiplexer_4 (.sel(ena), .in_0(1'b1), .in_1(clk), .out(Clk_in));
  and and_4 (and_4_out, rst_n, not_1_out);
  and and_5 (and_5_out, xor_1_out, execute_pulse);
  opcode_microcode_rom #(.applicationType("IVERILOG"), .CodeFile("D:\\Desktop\\fpga\\RemedyCpu\\verilog\\opcode_microcode_rom.v")) u_opcode_microcode_rom (
    .opcode(multiplexer_1_out), .muxb0(muxB[2]), .muxb1(muxB[1]), .muxb2(muxB[0]), .aluop0(aluOp[5]),
    .aluop1(aluOp[4]), .aluop2(aluOp[3]), .aluop3(aluOp[2]), .aluop4(aluOp[1]), .aluop5(aluOp[0]),
    .WE(u_opcode_microcode_rom_we), .sf(u_opcode_microcode_rom_sf), .iem0(iem[1]), .iem1(iem[0]),
    .br0(br[2]), .br1(br[1]), .br2(br[0]), .muxA(muxA), .ld(ld), .st(st), .abs(abs),
    .ioW(u_opcode_microcode_rom_iow), .ioR(u_opcode_microcode_rom_ior), .stPC(stPC), .Reti(Reti),
    .flash_req(flash_req), .BRK(Break));
  programCounter #(.applicationType("IVERILOG"), .CodeFile("C:\\Users\\Berkant\\Desktop\\fpga\\RemedyCpu\\verilog\\programCounter.v")) u_programCounter (
    .AluIn(AddrOut), .clk(Clk_in), .rst_n(and_4_out), .pc_en(pc_en), .absJmp(and_3_out), .intr(and_1_out),
    .reti(and_2_out), .deb_jump_addr(deb_jump_addr), .deb_jump(deb_jump_req), .relJmp(and_5_out),
    .PC(programAddr));
  debug_serial_frontend_tiny #(.applicationType("IVERILOG"), .CodeFile("D:\\Desktop\\fpga\\RemedyCpu\\verilog\\debug_serial_frontend_tiny_sync.v")) u_debug_serial_frontend_tiny (
    .cpu_clk(Clk_in), .rst_n(rst_n), .dbg_clk(dbg_clk), .dbg_data_in(dbg_data_in), .reg_rdata(reg_rdata),
    .dbg_data_out(dbg_data_out), .dbg_data_oe(dbg_data_oe), .reg_wr(u_debug_serial_frontend_tiny_reg_wr),
    .reg_addr(u_debug_serial_frontend_tiny_reg_addr), .reg_wdata(u_debug_serial_frontend_tiny_reg_wdata));
  Add #(.Bits(16)) add_1 (.a(programAddr), .b(16'h1), .c_i(1'b0), .s(add_1_s));  // open: c_o
  not not_2 (not_2_out, flash_req);
  not not_3 (not_3_out, ld);
  qspi_memory_interface #(.applicationType("IVERILOG"), .CodeFile("D:\\Desktop\\fpga\\RemedyCpu\\verilog\\qspi_memory_interface_flashqspi_ramspi_area_noramreset.v")) u_qspi_memory_interface (
    .clk(Clk_in), .spi_rst_n(rst_complex), .st(spi_st), .ld(spi_ld), .spi_target(spi_target),
    .addr(spi_addr), .data_in(spi_data_out), .spi_data_in({IO_in[5:4], IO_in[2:1]}), .data_out(spi_data),
    .spi_clk(IO_out[3]), .spi_flash_cs(IO_out[0]), .spi_ram_cs(IO_out[6]),
    .spi_data_out({IO_out[5:4], IO_out[2:1]}), .spi_data_oe({IO_oe[5:4], IO_oe[2:1]}), .busy(spi_busy_ram));
  or or_1 (or_1_out, not_2_out, not_3_out);
  or or_2 (or_2_out, flash_req, ld);
  and and_6 (sf, u_opcode_microcode_rom_sf, execute_pulse);
  and and_7 (ioW, u_opcode_microcode_rom_iow, execute_pulse);
  and and_8 (ioR, u_opcode_microcode_rom_ior, execute_pulse);
  and and_9 (and_9_out, or_1_out, execute_pulse, u_opcode_microcode_rom_we);
  and and_10 (and_10_out, u_opcode_microcode_rom_we, data_done, or_2_out);
  or or_3 (WE, and_9_out, and_10_out);
  or or_4 (or_4_out, flash_req, ld);
  muxEncoder #(.applicationType("IVERILOG"), .CodeFile("D:\\Desktop\\fpga\\RemedyCpu\\verilog\\multipleToMux-4.v")) u_muxEncoder (
    .a(1'b0), .b(or_4_out), .c(ioR), .d(stPC), .Q(u_muxEncoder_q));
  Multiplexer #(.Selector_Bits(2), .Bits(16)) multiplexer_5 (
    .sel(u_muxEncoder_q), .in_0(AddrOut), .in_1(mem_out), .in_2(iow_Din), .in_3(add_1_s),
    .out(multiplexer_5_out));
  Register #(.Bits(16)) register_1 (.D(mem_out), .C(Clk_in), .en(Fetch_done), .Q({imm, inst_reg}));
  debug_core_tiny #(.applicationType("IVERILOG"), .CodeFile("D:\\Desktop\\fpga\\RemedyCpu\\verilog\\debug_core_tiny_reset_jump.v")) u_debug_core_tiny (
    .clk(Clk_in), .rst_n(rst_n), .reg_wr(u_debug_serial_frontend_tiny_reg_wr),
    .reg_addr(u_debug_serial_frontend_tiny_reg_addr), .reg_wdata(u_debug_serial_frontend_tiny_reg_wdata),
    .cpu_dbg_halted(dbg_halted), .cpu_flags(flag_out), .cpu_pc(programAddr), .cpu_ir({imm, inst_reg}),
    .instr_is_brk(Break), .execute_now_pulse(execute_pulse), .reg_rdata(reg_rdata), .dbg_enable(dbg_en),
    .dbg_halt_req(halt_req), .dbg_run_req(run_req), .dbg_step_req(step_req),
    .static_break_enable(ststic_break_en), .dbg_break_hit(u_debug_core_tiny_dbg_break_hit),
    .dbg_break_after_exec(u_debug_core_tiny_dbg_break_after_exec), .dbg_soft_reset_req(soft_reset_req),
    .dbg_jump_req(deb_jump_req), .dbg_jump_addr(deb_jump_addr));
  xor xor_1 (xor_1_out, multiplexer_6_out, br[2]);
  Multiplexer #(.Selector_Bits(2)) multiplexer_6 (
    .sel(br[1:0]), .in_0(1'b0), .in_1(flag_out[2]), .in_2(flag_out[1]), .in_3(flag_out[0]),
    .out(multiplexer_6_out));
  and and_11 (and_11_out, ld, execute_pulse);
  and and_12 (and_12_out, execute_pulse, st);
  and and_13 (and_13_out, execute_pulse, flash_req);
  not not_4 (not_4_out, soft_reset_req);
  register_1bit NegR (.D(u_Alu_neg), .C(Clk_in), .en(sf), .rst(rst_n), .Q(flag_out[0]));
  register_1bit ZeroR (.D(u_Alu_zero), .C(Clk_in), .en(sf), .rst(rst_n), .Q(flag_out[1]));
  register_1bit CarryR (.D(u_Alu_carryout), .C(Clk_in), .en(sf), .rst(rst_n), .Q(flag_out[2]));
  and and_14 (rst_complex, rst_n, not_4_out);
  RegisterBlock #(.applicationType("IVERILOG"), .CodeFile("D:\\Desktop\\fpga\\RemedyCpu\\verilog\\reg16x16.v")) u_RegisterBlock (
    .DataIn(multiplexer_5_out), .WE(WE), .clk(Clk_in), .src(inst_reg[3:0]), .Dest(inst_reg[7:4]),
    .RDest(u_RegisterBlock_rdest), .Rsrc(DataOut));
  // ImReg imreg_1: pin names not known; wires that end beside it: imm, iem, Clk_in, {imm, inst_reg}, ImmReg
  memory_wait_controller_tiny #(.applicationType("IVERILOG"), .CodeFile("D:\\Desktop\\fpga\\RemedyCpu\\verilog\\memory_wait_controller_tiny.v")) u_memory_wait_controller_tiny (
    .clk(Clk_in), .rst_n(rst_complex), .fetch_req(fetch_request_pulse), .ld_req(and_11_out),
    .st_req(and_12_out), .flash_req(and_13_out), .fetch_addr(programAddr), .data_addr(AddrOut),
    .store_data(DataOut), .spi_data_out(spi_data), .spi_busy(spi_busy_ram), .mem_rdata(mem_out),
    .fetch_done(Fetch_done), .data_done(data_done), .mem_stall(u_memory_wait_controller_tiny_mem_stall),
    .spi_st(spi_st), .spi_ld(spi_ld), .spi_addr(spi_addr), .spi_data_in(spi_data_out), .spi_target(spi_target));
  // singExtend singextend_1: pin names not known; wires that end beside it: inst_reg[7:0], singextend_1_p2, singextend_1_p3, singextend_1_p4
  Multiplexer #(.Bits(16)) multiplexer_7 (
    .sel(muxA), .in_0(u_RegisterBlock_rdest), .in_1(DataOut), .out(multiplexer_7_out));
  Multiplexer #(.Selector_Bits(3), .Bits(16)) multiplexer_8 (
    .sel(muxB), .in_0(DataOut), .in_1({16{1'b0}}), .in_2(ImmReg), .in_3({16{1'b0}}), .in_4({16{1'b0}}),
    .in_5(singextend_1_p2), .in_6(singextend_1_p3), .in_7(singextend_1_p4), .out(multiplexer_8_out));
  and and_15 (and_15_out, AddrOut[2], AddrOut[1]);
  not not_5 (not_5_out, u_memory_wait_controller_tiny_mem_stall);
  cpu_cycle_controller_tiny #(.applicationType("IVERILOG"), .CodeFile("D:\\Desktop\\fpga\\RemedyCpu\\verilog\\cpu_cycle_controller_tiny.v")) u_cpu_cycle_controller_tiny (
    .clk(Clk_in), .rst_n(rst_complex), .fetch_done(Fetch_done), .data_done(data_done), .ld(ld), .st(st),
    .flash_ld(flash_req), .dbg_enable(dbg_en), .dbg_halt_req(halt_req), .dbg_run_req(run_req),
    .dbg_step_req(step_req), .dbg_break_hit(u_debug_core_tiny_dbg_break_hit),
    .dbg_break_after_exec(u_debug_core_tiny_dbg_break_after_exec), .fetch_req(fetch_request_pulse),
    .execute_now_pulse(execute_pulse), .dbg_halted(dbg_halted));
  and and_16 (and_16_out, AddrOut[3], not_8_out, not_9_out);
  or or_5 (or_7_out[0], and_19_out, and_18_out, and_16_out, and_15_out);
  and and_17 (pc_en, not_5_out, execute_pulse);
  and and_18 (and_18_out, AddrOut[3], not_9_out, AddrOut[0]);
  Alu #(.applicationType("IVERILOG"), .CodeFile("D:\\Desktop\\fpga\\RemedyCpu\\verilog\\alu.v")) u_Alu (
    .A(multiplexer_7_out), .B(multiplexer_8_out), .carryIn(flag_out[2]), .AluOp(aluOp), .Out(AddrOut),
    .Neg(u_Alu_neg), .Zero(u_Alu_zero), .CarryOut(u_Alu_carryout));
  and and_19 (and_19_out, not_6_out, not_8_out, not_9_out, AddrOut[0]);
  and and_20 (and_20_out, AddrOut[3], not_8_out, not_9_out);
  and and_21 (and_21_out, not_7_out, AddrOut[2]);
  Multiplexer #(.Selector_Bits(3), .Bits(16)) multiplexer_9 (
    .sel(or_7_out), .in_0({{8{1'b0}}, ui_in}), .in_1({{8{1'b0}}, outputToOutside, uo_out[5:0]}),
    .in_2(timerdat1), .in_3(timerdat2), .in_4(rngdat0), .in_5(intr_reg), .in_6(i2cDat), .in_7(i2cDat),
    .out(iow_Din));
  and and_22 (and_22_out, not_7_out, AddrOut[1]);
  or or_6 (or_7_out[1], AddrOut[4], and_22_out, and_21_out, and_20_out);
  and and_23 (and_23_out, AddrOut[3], AddrOut[2]);
  and and_24 (and_24_out, AddrOut[3], AddrOut[1], AddrOut[0]);
  or or_7 (or_7_out[2], AddrOut[4], and_24_out, and_23_out);
  not not_6 (not_6_out, AddrOut[4]);
  not not_7 (not_7_out, AddrOut[3]);
  not not_8 (not_8_out, AddrOut[2]);
  not not_9 (not_9_out, AddrOut[1]);
  lfsr_RandomNumberGen #(.applicationType("IVERILOG"), .CodeFile("D:\\Desktop\\fpga\\RemedyCpu\\verilog\\lfsr.v")) u_lfsr_RandomNumberGen (
    .adrrIn(AddrOut[4:0]), .dataIn(DataOut[7:0]), .ioW(ioW), .clk(Clk_in), .SeedAdr(5'b01011),
    .RngAdr(5'b01100), .Out(rngdat0));
  Comparator #(.Bits(5)) comparator_1 (.a(AddrOut[4:0]), .b(5'b00001), .eq(comparator_1_eq));  // open: gt, lt
  and and_25 (and_25_out, AddrOut[4], ioW);
  timer #(.applicationType("IVERILOG"), .CodeFile("D:\\Desktop\\fpga\\RemedyCpu\\verilog\\timer_small.v")) u_timer (
    .dOut(DataOut), .Addr(AddrOut[4:0]), .ioW(ioW), .C(Clk_in), .InterLock(InterLock),
    .timerConfigAddr(5'b00010), .timerTargetAddr(5'b00011), .timerResetAddr(5'b00100),
    .timerReadAddr(5'b00101), .timerSyncStartAddr(5'b01010), .rst_n(rst_n), .TimerOut(timerdat1),
    .timer_interrupt(u_timer_tiny_timer_interrupt[0]));
  timer_tiny #(.applicationType("IVERILOG"), .CodeFile("D:\\Desktop\\fpga\\RemedyCpu\\verilog\\timer_tiny.v")) u_timer_tiny (
    .dOut(DataOut[8:0]), .Addr(AddrOut[4:0]), .ioW(ioW), .C(Clk_in), .InterLock(InterLock),
    .timerConfigAddr(5'b00110), .timerTargetAddr(5'b00111), .timerResetAddr(5'b01000),
    .timerReadAddr(5'b01001), .timerSyncStartAddr(5'b01010), .rst_n(rst_n), .TimerOut(timerdat2),
    .timer_interrupt(u_timer_tiny_timer_interrupt[1]));
  and and_26 (and_26_out, comparator_1_eq, ioW);
  interrupt_controller_small #(.applicationType("IVERILOG"), .CodeFile("D:\\Desktop\\fpga\\RemedyCpu\\verilog\\interrupt_controller.v")) u_interrupt_controller_small (
    .dOut(DataOut[3:0]), .Addr(AddrOut[4:0]), .ioW(ioW), .C(Clk_in), .rst_n(rst_complex),
    .irq_in({i2c_inter, u_timer_tiny_timer_interrupt}), .imm(imm), .reti(Reti), .pc_en(pc_en),
    .CPUInterruptEnableAddr(5'b01101), .inputInterruptAddr(5'b01110), .interruptRegAddr(5'b01111),
    .InterruptOut(intr_reg), .intr(intr), .irq_lock(InterLock));
  i2c_master_ctrl #(.applicationType("IVERILOG"), .CodeFile("D:\\Desktop\\fpga\\RemedyCpu\\verilog\\i2c_master_ctrl_min.v")) u_i2c_master_ctrl (
    .clk(Clk_in), .rst_n(rst_n), .wr_en(and_25_out), .reg_addr(AddrOut[3:0]), .cpu_din(DataOut),
    .sda_in(IO_in[7]), .cpu_dout(i2cDat), .sda_out(IO_out[7]), .scl_out(scl_o), .scl_oe(scl_oe),
    .sda_oe(IO_oe[7]), .interrupt(i2c_inter));
  register_8bit outputReg (
    .D(DataOut[7:0]), .C(Clk_in), .en(and_26_out), .rst(rst_n), .Q({outputToOutside, uo_out[5:0]}));

  // Other names for the same wires on the sheet: OPcode[7:0] = {imm, inst_reg[14:8]}; inst_reg[15] = imm;
  //   qspi_data_in[3:0] = {IO_in[5:4], IO_in[2:1]}; sda_in = IO_in[7]; outputToOutside[5:0] = uo_out[5:0];
  //   outR[7:0] = {outputToOutside, uo_out[5:0]}; qspi_data_oe[3:0] = {IO_oe[5:4], IO_oe[2:1]};
  //   qspi_data_out[3:0] = {IO_out[5:4], IO_out[2:1]}; rst = rst_n; sda_o = IO_out[7]; sda_oe = IO_oe[7];
  //   spi_clock = IO_out[3]; spics_flash = IO_out[0]; spics_ram = IO_out[6]; inputFromOutside[7:0] = ui_in;
  //   inputReg[7:0] = ui_in

  // Notes on the sheet:
  //   clk: Hz: 20
  //   ena: default 1
  //   Input/Output
  //   ControlLogic
  //   ProgramMemoryRead
  //   JumpLogic
  //   FlagStore
  //   IO Addresses
  //   PERIPHERAL ADDRESSES
  //   Write/Read Addresses
  //   PERIPHERAL BUS
  //   RandomNumberGen
  //   Timers
  //   input
  //   Output
  //   InterruptBus
  //   INTERRRRRUPT BUS
endmodule
